# Fritzing sketch BEVO_IAQ (saved by Fritzing 0.9.3b)
circuit board: 5.06347cm x 2.64627cm
breadboards: 1

parts:
  Raspberry_Pi_1 = Raspberry Pi 3 [part_number=RPI-3-V1.2]
  SCL_Pull-Up = Resistor [tolerance=±5% resistance=4.7k package="2512 [SMD]"]
  SCD30 = Triple Axis Gyro Breakout ITG-3200
  SVM30 = Header 4 [package=molex-1x4_lock]
  SPS30 = Adafruit SGP30 Gas Sensor
  SDA_Pull-Up = Resistor [tolerance=±5% resistance=4.7k package="2512 [SMD]"]
  TSL = Adafruit TSL2591 [part_number="Adafruit #1980"]
  RTC = Adafruit PCF8523 RTC [part_number="Adafruit #3295"]

nets:
  N1: Raspberry_Pi_1.GPIO2, SCD30.INT, SVM30.1, SPS30.SCL, SDA_Pull-Up.Pin_0, TSL.SDA, RTC.SDA
  GND: Raspberry_Pi_1.GPIO3, SCL_Pull-Up.Pin_0, SCD30.GND, SVM30.4, SPS30.GND, TSL.SCL, RTC.SCL
  GND_2: Raspberry_Pi_1.GND, SCD30.VLOGIC, SCD30.SCL, SVM30.3, SPS30.VIN, SPS30.V+, TSL.GND, RTC.GND
  VCC: Raspberry_Pi_1.5V, SCL_Pull-Up.Pin_1, SCD30.VCC, SVM30.2, SPS30.SDA, SDA_Pull-Up.Pin_1, TSL.VIN, RTC.VCC

custom parts:
  Adafruit TSL2591: When the future is dazzlingly-bright, this ultra-high-range luminosity sensor will help you measure it. The TSL2591 luminosity sensor is an advanced digital light sensor, ideal for use in a wide range of light situations. Compared to low cost CdS cells, this sensor is more precise, allowing for exact lux calculations and can be configured for different gain/timing ranges to detect light ranges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
  Adafruit PCF8523 RTC: This is a great battery-backed real time clock (RTC) that allows your microcontroller project to keep track of time even if it is reprogrammed, or if the power is lost. Perfect for datalogging, clock-building, time stamping, timers and alarms, etc. Equipped with PCF8523 RTC - it can run from 3.3V or 5V power & logic! Works great with an Arduino using our RTC library, with CircuitPython or with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
