# Fritzing sketch PCF8523 (saved by Fritzing 0.9.3b)
breadboards: 1

parts:
  Part1 = Adafruit PCF8523 RTC [part_number="Adafruit #3295"]
  Raspberry_Pi_1 = Raspberry Pi 3 [part_number=RPI-3-V1.2]
  R1 = Resistor [tolerance=±5% resistance=4.7k package="2512 [SMD]"]
  R2 = Resistor [tolerance=±5% resistance=4.7k package="2512 [SMD]"]

nets:
  N1: Part1.SCL, Raspberry_Pi_1.GPIO3, R2.Pin_0
  N2: Part1.SDA, Raspberry_Pi_1.GPIO2, R1.Pin_0
  VCC: Part1.VCC, Raspberry_Pi_1.5V, R1.Pin_1, R2.Pin_1
  GND: Part1.GND, Raspberry_Pi_1.GND

custom parts:
  Adafruit PCF8523 RTC: This is a great battery-backed real time clock (RTC) that allows your microcontroller project to keep track of time even if it is reprogrammed, or if the power is lost. Perfect for datalogging, clock-building, time stamping, timers and alarms, etc. Equipped with PCF8523 RTC - it can run from 3.3V or 5V power & logic! Works great with an Arduino using our RTC library, with CircuitPython or with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
