# Fritzing sketch SCD30 (saved by Fritzing 0.9.3b)
breadboards: 1

parts:
  Raspberry_Pi1 = Raspberry Pi B+
  Part1 = Adafruit SHT31-D Sensirion Temperature/Humidity Sensor [part_number="Adafruit #2857"]
  R1 = Resistor [tolerance=±5% resistance=4.7 package=THT]
  R2 = Resistor [tolerance=±5% resistance=4.7 package=THT]

nets:
  3V3: Raspberry_Pi1.3v3, Raspberry_Pi1.3V3, Part1.VIN, R1.Pin_0, R2.Pin_0
  N1: Raspberry_Pi1.GPIO2, Part1.SDA, R2.Pin_1
  N2: Raspberry_Pi1.GPIO3, Part1.SCL, R1.Pin_1
  GND: Raspberry_Pi1.GND, Part1.GND, Part1.ALERT

custom parts:
  Adafruit SHT31-D Sensirion Temperature/Humidity Sensor: Sensirion Temperature/Humidity sensors are some of the finest & highest-accuracy devices you can get. And, finally we have some that have a true I2C interface for easy reading. The SHT31-D sensor has an excellent ±2% relative humidity and ±0.3°C accuracy for most uses. Unlike earlier SHT sensors, this sensor has a true I2C interface, and (bonus!) even with two address options. It also is 3V or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
