# Fritzing sketch TSL2591 (saved by Fritzing 0.9.3b)
breadboards: 1

parts:
  Part1 = Adafruit TSL2591 [part_number="Adafruit #1980"]
  Raspberry_Pi_1 = Raspberry Pi 3 [part_number=RPI-3-V1.2]
  R1 = Resistor [tolerance=±5% resistance=4.7k package="0805 [SMD]"]
  R2 = Resistor [tolerance=±5% resistance=4.7k package="0805 [SMD]"]

nets:
  VIN: Part1.VIN, Raspberry_Pi_1.5V, R1.Pin_1, R2.Pin_1
  GND: Part1.GND, Raspberry_Pi_1.GND
  N1: Part1.SDA, Raspberry_Pi_1.GPIO2, R1.Pin_0
  N2: Part1.SCL, Raspberry_Pi_1.GPIO3, R2.Pin_0

custom parts:
  Adafruit TSL2591: When the future is dazzlingly-bright, this ultra-high-range luminosity sensor will help you measure it. The TSL2591 luminosity sensor is an advanced digital light sensor, ideal for use in a wide range of light situations. Compared to low cost CdS cells, this sensor is more precise, allowing for exact lux calculations and can be configured for different gain/timing ranges to detect light ranges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
